// Logisim project olaf2.circ as structural Verilog
module main (
  input  RST
);

  wire CLK_out, cpu_1_rst_out, or_1_out;
  wire [7:0] cpu_1_ip;
  wire [15:0] rom_1_data;

  Clock CLK (.out(CLK_out));
  or or_1 (or_1_out, cpu_1_rst_out, RST);
  CPU cpu_1 (.CLK(CLK_out), .RST_IN(or_1_out), .OPCODE(rom_1_data), .IP(cpu_1_ip), .RST_OUT(cpu_1_rst_out));
  ROM #(.dataWidth(16)) rom_1 (.addr(cpu_1_ip), .data(rom_1_data), .sel(1'b1));

  // Notes on the sheet:
  //   contents of rom_1 (hex, n*v repeats v):
  //   61b 508 41b 501 1f
endmodule

module ALU (
  input  [7:0] SOURCE,
  input  [7:0] DEST,
  input  ADD,
  input  SUB,
  input  MUL,
  input  DIV,
  input  SHL,
  input  SHR,
  input  NOT,
  input  AND,
  input  OR,
  input  XOR,
  output CARRY,
  output BORROW,
  output ZERO,
  output [7:0] OUT,
  output [7:0] MOD,
  output ALU_USED
);

  wire not_2_out, not_3_out, not_4_out, not_5_out, not_6_out, not_7_out, not_8_out, not_9_out;
  wire [2:0] controlled_buffer_6_out, pull_resistor_4_node;
  wire [7:0] adder_1_out, and_1_out, controlled_buffer_1_out, controlled_buffer_3_out,
       controlled_buffer_5_out, controlled_buffer_8_out, controlled_buffer_9_out, controlled_buffer_10_out,
       controlled_buffer_11_out, controlled_buffer_14_out, controlled_buffer_15_out,
       controlled_buffer_16_out, controlled_buffer_17_out, controlled_buffer_18_out,
       controlled_buffer_19_out, divider_1_out, multiplier_1_out, not_1_out, or_2_out, pull_resistor_2_node,
       pull_resistor_7_node, pull_resistor_12_node, pull_resistor_13_node, shifter_1_out, shifter_2_out,
       subtractor_1_out, xor_1_out;

  or or_1 (ALU_USED, ADD, SUB, MUL, DIV, SHL, SHR, NOT, AND, OR, XOR);
  assign controlled_buffer_1_out = SUB ? SOURCE : 8'bz;  // Controlled_Buffer controlled_buffer_1
  Pull_Resistor pull_resistor_1 (.node(controlled_buffer_1_out));
  Pull_Resistor pull_resistor_2 (.node(pull_resistor_2_node));
  assign pull_resistor_2_node = SUB ? DEST : 8'bz;  // Controlled_Buffer controlled_buffer_2
  assign controlled_buffer_3_out = SHL ? SOURCE : 8'bz;  // Controlled_Buffer controlled_buffer_3
  Pull_Resistor pull_resistor_3 (.node(controlled_buffer_3_out));
  Pull_Resistor pull_resistor_4 (.node(pull_resistor_4_node));
  assign pull_resistor_4_node = SHL ? DEST[2:0] : 3'bz;  // Controlled_Buffer controlled_buffer_4
  assign controlled_buffer_5_out = SHR ? SOURCE : 8'bz;  // Controlled_Buffer controlled_buffer_5
  Pull_Resistor pull_resistor_5 (.node(controlled_buffer_5_out));
  assign controlled_buffer_6_out = SHR ? DEST[2:0] : 3'bz;  // Controlled_Buffer controlled_buffer_6
  Pull_Resistor pull_resistor_6 (.node(controlled_buffer_6_out));
  Pull_Resistor #(.pull(1)) pull_resistor_7 (.node(pull_resistor_7_node));
  assign pull_resistor_7_node = NOT ? SOURCE : 8'bz;  // Controlled_Buffer controlled_buffer_7
  assign controlled_buffer_8_out = AND ? SOURCE : 8'bz;  // Controlled_Buffer controlled_buffer_8
  Pull_Resistor pull_resistor_8 (.node(controlled_buffer_8_out));
  assign controlled_buffer_9_out = AND ? DEST : 8'bz;  // Controlled_Buffer controlled_buffer_9
  Pull_Resistor pull_resistor_9 (.node(controlled_buffer_9_out));
  assign controlled_buffer_10_out = OR ? SOURCE : 8'bz;  // Controlled_Buffer controlled_buffer_10
  Pull_Resistor pull_resistor_10 (.node(controlled_buffer_10_out));
  assign controlled_buffer_11_out = OR ? DEST : 8'bz;  // Controlled_Buffer controlled_buffer_11
  Pull_Resistor pull_resistor_11 (.node(controlled_buffer_11_out));
  Pull_Resistor pull_resistor_12 (.node(pull_resistor_12_node));
  assign pull_resistor_12_node = XOR ? SOURCE : 8'bz;  // Controlled_Buffer controlled_buffer_12
  Pull_Resistor pull_resistor_13 (.node(pull_resistor_13_node));
  assign pull_resistor_13_node = XOR ? DEST : 8'bz;  // Controlled_Buffer controlled_buffer_13
  assign controlled_buffer_14_out = ADD ? SOURCE : 8'bz;  // Controlled_Buffer controlled_buffer_14
  Adder adder_1 (
    .a(controlled_buffer_14_out), .b(controlled_buffer_15_out), .out(adder_1_out), .cout(CARRY));  // open: cin
  assign controlled_buffer_15_out = ADD ? DEST : 8'bz;  // Controlled_Buffer controlled_buffer_15
  Subtractor subtractor_1 (
    .a(controlled_buffer_1_out), .b(pull_resistor_2_node), .out(subtractor_1_out), .bin(1'b0), .bout(BORROW));
  assign controlled_buffer_16_out = MUL ? SOURCE : 8'bz;  // Controlled_Buffer controlled_buffer_16
  Multiplier multiplier_1 (
    .a(controlled_buffer_16_out), .b(controlled_buffer_17_out), .out(multiplier_1_out), .cin({8{1'b0}}));  // open: cout
  assign controlled_buffer_17_out = MUL ? DEST : 8'bz;  // Controlled_Buffer controlled_buffer_17
  assign controlled_buffer_18_out = DIV ? SOURCE : 8'bz;  // Controlled_Buffer controlled_buffer_18
  Divider divider_1 (
    .a(controlled_buffer_18_out), .b(controlled_buffer_19_out), .out(divider_1_out), .upper({8{1'b0}}),
    .rem(MOD));
  assign controlled_buffer_19_out = DIV ? DEST : 8'bz;  // Controlled_Buffer controlled_buffer_19
  Shifter shifter_1 (.in(controlled_buffer_3_out), .\dist (pull_resistor_4_node), .out(shifter_1_out));
  Shifter #(.shift("lr")) shifter_2 (
    .in(controlled_buffer_5_out), .\dist (controlled_buffer_6_out), .out(shifter_2_out));
  assign not_1_out = ~pull_resistor_7_node;  // NOT_Gate not_1, 8 bits wide
  assign and_1_out = controlled_buffer_8_out & controlled_buffer_9_out;  // AND_Gate and_1, 8 bits wide
  assign or_2_out = controlled_buffer_10_out | controlled_buffer_11_out;  // OR_Gate or_2, 8 bits wide
  assign xor_1_out = pull_resistor_12_node ^ pull_resistor_13_node;  // XOR_Gate xor_1, 8 bits wide
  Pull_Resistor pull_resistor_14 (.node(CARRY));
  Pull_Resistor pull_resistor_15 (.node(BORROW));
  Pull_Resistor pull_resistor_16 (.node(adder_1_out));
  Pull_Resistor pull_resistor_17 (.node(multiplier_1_out));
  Pull_Resistor pull_resistor_18 (.node(divider_1_out));
  Pull_Resistor pull_resistor_19 (.node(shifter_1_out));
  ExactlyOne xor_2[7:0] (
    .out(OUT), .in0(adder_1_out), .in1(subtractor_1_out), .in2(multiplier_1_out), .in3(divider_1_out),
    .in4(shifter_1_out), .in5(shifter_2_out), .in6(not_1_out), .in7(and_1_out), .in8(or_2_out),
    .in9(xor_1_out));
  Pull_Resistor pull_resistor_20 ();  // open: node
  Pull_Resistor pull_resistor_21 (.node(not_1_out));
  Pull_Resistor pull_resistor_22 (.node(and_1_out));
  Pull_Resistor pull_resistor_23 (.node(or_2_out));
  Pull_Resistor pull_resistor_24 (.node(xor_1_out));
  Pull_Resistor pull_resistor_25 (.node(MOD));
  Pull_Resistor pull_resistor_26 (.node(OUT));
  not not_2 (not_2_out, OUT[0]);
  not not_3 (not_3_out, OUT[1]);
  not not_4 (not_4_out, OUT[2]);
  not not_5 (not_5_out, OUT[3]);
  not not_6 (not_6_out, OUT[4]);
  not not_7 (not_7_out, OUT[5]);
  not not_8 (not_8_out, OUT[6]);
  not not_9 (not_9_out, OUT[7]);
  and and_2 (ZERO, not_2_out, not_3_out, not_4_out, not_5_out, not_6_out, not_7_out, not_8_out, not_9_out);
endmodule

module CPU (
  input  CLK,
  input  RST_IN,
  input  [15:0] OPCODE,
  output RST_OUT,
  output [7:0] IP
);

  wire alu_1_alu_used, and_1_out, decoder_1_out1, decoder_1_out2, decoder_1_out3, decoder_1_out4,
       decoder_1_out5, decoder_1_out6, decoder_1_out7, decoder_1_out8, decoder_1_out9, decoder_1_out10,
       decoder_1_out11, decoder_1_out12, decoder_1_out27, flags_1_borrow, flags_1_carry, flags_1_zero,
       not_1_out, or_1_out, or_4_out, or_5_out;
  wire [2:0] flags_1_ip_reg, or_2_out;
  wire [7:0] alu_1_mod, alu_1_out, multiplexer_1_out, or_3_out, regs_1_ra, regs_1_rb, regs_1_rc, regs_1_rd,
       regs_1_sp;

  Decoder #(.select(5), .enable("false")) decoder_1 (
    .out1(decoder_1_out1), .out2(decoder_1_out2), .out3(decoder_1_out3), .out4(decoder_1_out4),
    .out5(decoder_1_out5), .out6(decoder_1_out6), .out7(decoder_1_out7), .out8(decoder_1_out8),
    .out9(decoder_1_out9), .out10(decoder_1_out10), .out11(decoder_1_out11), .out12(decoder_1_out12),
    .out27(decoder_1_out27), .out31(RST_OUT), .sel(OPCODE[4:0]));  // open: out0, out13, out14, out15, out16, out17, out18, out19, out20, out21, out22, out23, out24, out25, out26, out28, out29, out30
  or or_1 (or_1_out, decoder_1_out2, decoder_1_out12);
  assign or_2_out = flags_1_ip_reg | OPCODE[7:5];  // OR_Gate or_2, 3 bits wide
  assign or_3_out = OPCODE[15:8] | alu_1_out;  // OR_Gate or_3, 8 bits wide
  or or_4 (or_4_out, decoder_1_out4, decoder_1_out5);
  FLAGS flags_1 (
    .BORROW(flags_1_borrow), .CARRY(flags_1_carry), .ZERO(flags_1_zero), .IP_REG(flags_1_ip_reg));  // open: JMP, JEQ, JNE, JBT, JST, JBE, JLE, JMP_OUT
  REGS regs_1 (
    .CLK(CLK), .RST(RST_IN), .REG(or_2_out), .VAL(or_3_out), .MOV(or_5_out), .RA(regs_1_ra), .RB(regs_1_rb),
    .RC(regs_1_rc), .RD(regs_1_rd), .IP(IP), .SP(regs_1_sp));
  or or_5 (or_5_out, decoder_1_out27, and_1_out);
  ALU alu_1 (
    .SOURCE(multiplexer_1_out), .DEST(OPCODE[15:8]), .ADD(decoder_1_out1), .SUB(or_1_out),
    .MUL(decoder_1_out3), .DIV(or_4_out), .SHL(decoder_1_out6), .SHR(decoder_1_out7), .NOT(decoder_1_out9),
    .AND(decoder_1_out10), .OR(decoder_1_out11), .XOR(decoder_1_out8), .CARRY(flags_1_carry),
    .BORROW(flags_1_borrow), .ZERO(flags_1_zero), .OUT(alu_1_out), .MOD(alu_1_mod), .ALU_USED(alu_1_alu_used));
  and and_1 (and_1_out, alu_1_alu_used, not_1_out);
  not not_1 (not_1_out, decoder_1_out12);
  Multiplexer #(.select(3), .width(8), .enable("false")) multiplexer_1 (
    .in0(regs_1_ra), .in1(regs_1_rb), .in2(regs_1_rc), .in3(regs_1_rd), .in4(IP), .in5(regs_1_sp),
    .out(multiplexer_1_out), .sel(or_2_out));  // open: in6, in7
  DotMatrix #(.matrixrows(8)) dotmatrix_1 (
    .col0(multiplexer_1_out), .col1(OPCODE[15:8]), .col2(alu_1_out), .col3(alu_1_mod));  // open: col4

  // Notes on the sheet:
  //   OPCODE: pull=down
endmodule

module FLAGS (
  input  JMP,
  input  JEQ,
  input  JNE,
  input  JBT,
  input  JST,
  input  JBE,
  input  JLE,
  output BORROW,
  output CARRY,
  output ZERO,
  output JMP_OUT,
  output [2:0] IP_REG
);

  wire and_1_out;

  and and_1 (and_1_out, JEQ, ZERO);
  or or_1 (JMP_OUT, JMP, and_1_out);

  assign IP_REG = 3'b110;

  // Notes on the sheet:
  //   JBE: pull=down
  //   JLE: pull=down
  //   JEQ: pull=down
  //   ZERO: pull=down
  //   CARRY: pull=down
  //   BORROW: pull=down
  //   JST: pull=down
  //   JMP: pull=down
  //   JNE: pull=down
  //   JBT: pull=down
endmodule

module REGS (
  input  CLK,
  input  RST,
  input  [2:0] REG,
  input  [7:0] VAL,
  input  MOV,
  output [7:0] RA,
  output [7:0] RB,
  output [7:0] RC,
  output [7:0] RD,
  output [7:0] IP,
  output [7:0] SP
);

  wire decoder_1_out0, decoder_1_out1, decoder_1_out2, decoder_1_out3, decoder_1_out4, decoder_1_out5,
       not_1_out;

  Pull_Resistor pull_resistor_1 (.node(MOV));
  Decoder #(.select(3), .disabled(0)) decoder_1 (
    .out0(decoder_1_out0), .out1(decoder_1_out1), .out2(decoder_1_out2), .out3(decoder_1_out3),
    .out4(decoder_1_out4), .out5(decoder_1_out5), .sel(REG), .en(MOV));  // open: out6, out7
  Register u_RA (.D(VAL), .en(decoder_1_out0), .Q(RA), .clk(CLK), .clr(RST));
  Register u_RB (.D(VAL), .en(decoder_1_out1), .Q(RB), .clk(CLK), .clr(RST));
  Register u_RC (.D(VAL), .en(decoder_1_out2), .Q(RC), .clk(CLK), .clr(RST));
  Counter u_IP (.load(decoder_1_out4), .D(VAL), .count(not_1_out), .Q(IP), .clk(CLK), .clr(RST));  // open: carry
  Register u_RD (.D(VAL), .en(decoder_1_out3), .Q(RD), .clk(CLK), .clr(RST));
  not not_1 (not_1_out, decoder_1_out4);
  Register u_SP (.D(VAL), .en(decoder_1_out5), .Q(SP), .clk(CLK), .clr(RST));

  // Notes on the sheet:
  //   CLK: pull=down
  //   REG: pull=down
  //   RST: pull=down
  //   MOV: pull=down
endmodule
